// Logisim project h.circ as structural Verilog: 1 circuit, main circuit main
module main (
);

  wire clock_1_out, nand_1_out, nand_2_out, nand_3_out, nand_4_out, nor_1_out, nor_2_out, nor_3_out,
       nor_4_out, not_1_out, not_2_out, not_3_out, not_4_out;
  wire [2:0] counter_1_q;

  Counter #(.width(3), .max('h5)) counter_1 (.Q(counter_1_q), .clk(clock_1_out));  // open: load, D, count, carry, clr
  Clock clock_1 (.out(clock_1_out));
  nand nand_1 (nand_1_out, counter_1_q[0], counter_1_q[1]);
  nand nand_2 (nand_2_out, counter_1_q[2], counter_1_q[2]);
  nor nor_1 (nor_1_out, counter_1_q[0], counter_1_q[1]);
  nand nand_3 (nand_3_out, nand_1_out, nand_2_out);
  nor nor_2 (nor_2_out, nor_1_out, nor_1_out);
  nand nand_4 (nand_4_out, counter_1_q[0], counter_1_q[2]);
  nor nor_3 (nor_3_out, nand_3_out, nand_3_out);
  nor nor_4 (nor_4_out, nor_2_out, counter_1_q[2]);
  not not_1 (not_1_out, counter_1_q[0]);
  not not_2 (not_2_out, nor_3_out);
  not not_3 (not_3_out, nor_4_out);
  not not_4 (not_4_out, nand_4_out);
  LED led_1 (.in(not_3_out));
  LED led_2 (.in(not_4_out));
  LED led_3 (.in(not_2_out));
  LED led_4 (.in(not_1_out));
  LED led_5 (.in(not_2_out));
  LED led_6 (.in(not_4_out));
  LED led_7 (.in(not_3_out));

  // Notes on the sheet:
  //   Qa
  //   Qb
  //   Qc
  //   74LS00
  //   D
  //   C
  //   B
  //   A
  //   74HC02
endmodule
